# Fritzing sketch Untitled Sketch (saved by Fritzing 0.9.3b)

parts:
  R1 = Resistor [tolerance=±5% resistance=220 package="0603 [SMD]"]
  R2 = Resistor [tolerance=±5% resistance=220 package="0805 [SMD]"]
  LED1 = smd LED [color="Red (633nm)" package="0603 [SMD]"]  # not connected
  LED2 = smd LED [color="Red (633nm)" package="0603 [SMD]"]
  WeMos_D1_Mini1 = WeMos D1 Mini
  KY-1 = Keyes Relay [package=THT]
  KY-2 = Keyes Relay [package=THT]
  DHT1 = DHT11 Humitidy and Temperature Sensor

nets:
  N1: R1.Pin_0, KY-2.NO
  N2: R2.Pin_0, KY-1.NO
  N3: LED2.cathode, KY-1.ground
  5V: WeMos_D1_Mini1.5V, DHT1.VDD
  N4: WeMos_D1_Mini1.D1, DHT1.DATA
  N5: WeMos_D1_Mini1.D3, KY-1.power
  N6: WeMos_D1_Mini1.D4, KY-2.power
  N7: WeMos_D1_Mini1.G, DHT1.GND

custom parts:
  Keyes Relay: The Keyes 5V relay module is suitable for SCM development, home appliance control. It uses a 5V~12V TIL control signal which can control DC / AC signal.
  DHT11 Humitidy and Temperature Sensor: DHT11 Humidity and Temperature Sensor
